# Fritzing sketch circuit (saved by Fritzing 0.9.9b)
breadboards: 1

parts:
  パーツ1 = Arduino Uno (Rev3)
  RE1 = Rotary Encoder [package=THT]

nets:
  N1: パーツ1.D8, RE1.EncoderPinA
  N2: パーツ1.GND, RE1.EncoderPinC
  N3: パーツ1.D6_PWM, RE1.EncoderPinB
